// Logisim project pc.circ as structural Verilog: 2 circuits, main circuit main
module main (
  input  in_1,
  input  PCSrc,
  input  [11:0] Imm
);

  wire clock_1_out;
  wire [31:0] adder_1_out, adder_2_out, extend_1_extended, multiplexer_1_out, register_1_q;

  Clock clock_1 (.out(clock_1_out));
  Register #(.width(32)) register_1 (
    .D(multiplexer_1_out), .clk(clock_1_out), .Q(register_1_q), .clr(in_1));  // open: en
  Extend extend_1 (.Offset(Imm), .Extended(extend_1_extended));
  Adder #(.width(32)) adder_1 (.a(register_1_q), .b(32'h4), .out(adder_1_out));  // open: cin, cout
  Adder #(.width(32)) adder_2 (.a(extend_1_extended), .b(register_1_q), .out(adder_2_out));  // open: cin, cout
  Multiplexer #(.width(32)) multiplexer_1 (.in0(adder_1_out), .in1(adder_2_out), .out(multiplexer_1_out), .sel(PCSrc));

  // Notes on the sheet:
  //   (Teilschaltungen können per Drag&Drop reingezogen werden)
  //   Mittels PCSrc wird zwischen der Addition mit 4 (d.h. eine Instruktion weiter)
  //   und der Addition mit unserem erweiterten Immediate (d.h. ein Sprung) gewählt
endmodule

module Extend (
  input  [11:0] Offset,
  output [31:0] Extended
);

  assign Extended[31:1] = {{19{Offset[11]}}, Offset};  // Bit_Extender bit_extender_1

  assign Extended[0] = 1'b0;

  // Notes on the sheet:
  //   Wir erweitern unseren 12-Bit immediate mit Vorzeichen auf 31 Bit,
  //   anschließend kombinieren wir diese 31-Bit-Zahl mit einer konstanten 0 zur
  //   32-Bit erweiterten Zahl
endmodule
