// Logisim project state_machine.circ as structural Verilog: 1 circuit, main circuit main
module main (
  input  Input,
  input  Reset,
  output Output
);

  wire and_1_out, and_2_out, and_3_out, clock_1_out, d_ff_1_q, d_ff_2_q, not_1_out, not_2_out, not_3_out,
       or_1_out;

  Clock clock_1 (.out(clock_1_out));
  not not_1 (not_1_out, Input);
  and and_1 (and_1_out, not_1_out, d_ff_2_q, not_2_out);
  not not_2 (not_2_out, d_ff_1_q);
  and and_2 (and_2_out, not_1_out, d_ff_2_q, d_ff_1_q);
  not not_3 (not_3_out, d_ff_2_q);
  and and_3 (and_3_out, Input, not_3_out, d_ff_1_q);
  or or_1 (or_1_out, and_1_out, and_2_out, and_3_out);
  D_Flip_Flop d_ff_1 (.D(or_1_out), .clk(clock_1_out), .Q(d_ff_1_q), .reset(Reset));  // open: Qn, preset
  D_Flip_Flop d_ff_2 (.D(Input), .clk(clock_1_out), .Q(d_ff_2_q), .reset(Reset));  // open: Qn, preset
  and and_4 (Output, d_ff_1_q, d_ff_2_q);

  // Notes on the sheet:
  //   CLK
  //   FF1
  //   FF0
endmodule
