// Digital circuit abs.dig as structural Verilog
module abs (
  input  a1,
  input  a0,
  input  b1,
  input  b0,
  output y0,
  output y1
);

  wire add_1_c_o, add_1_s, add_2_c_o, add_2_s, add_3_c_o, add_3_s, add_4_s, not_1_out, not_2_out, not_3_out,
       not_4_out, not_5_out;

  not not_1 (not_1_out, b0);
  not not_2 (not_2_out, b1);
  Add add_1 (.a(a0), .b(not_1_out), .c_i(1'b1), .s(add_1_s), .c_o(add_1_c_o));
  Add add_2 (.a(a1), .b(not_2_out), .c_i(add_1_c_o), .s(add_2_s), .c_o(add_2_c_o));
  not not_3 (not_3_out, add_2_c_o);
  not not_4 (not_4_out, add_1_s);
  not not_5 (not_5_out, add_2_s);
  Add add_3 (.a(not_4_out), .b(1'b0), .c_i(1'b1), .s(add_3_s), .c_o(add_3_c_o));
  Add add_4 (.a(not_5_out), .b(1'b0), .c_i(add_3_c_o), .s(add_4_s));  // open: c_o
  Multiplexer multiplexer_1 (.sel(not_3_out), .in_0(add_1_s), .in_1(add_3_s), .out(y0));
  Multiplexer multiplexer_2 (.sel(not_3_out), .in_0(add_2_s), .in_1(add_4_s), .out(y1));

  // Notes on the sheet:
  //   Schritt 1
  //   1. Wir berechnen die Subtraktion
  //   (a-b) mit einem Volladdierer, wie
  //   in der VL gezeigt. Dafür wird b implizit
  //   in ein 3-Bit-Zweierkomplement
  //   übertragen.
  //   2. Da das implizite Bit b2 immer 
  //   0 ist, müsste cout des zweiten
  //   Addierers mit 1 addiert werden,
  //   um das Vorzeichen (= 3. Ausgangsbit)
  //   zu erhalten. Da uns allerdings
  //   nur das Vorzeichen interessiert,
  //   reicht ein NOT-Gatter.
  //   Schritt 2
  //   Schritt 3
  //   3. Falls das Vorzeichenbit gesetzt ist,
  //   haben wir eine negative Zahl (im 
  //   ZK) am Ausgang. Da wir allerdings den
  //   Absolutbetrag wollen, müssen wir im
  //   Falle eines negativen Ergebnisses
  //   wieder das ZK anwenden, um den
  //   Absolutbetrag zu bekommen
  //   Schritt 4
  //   4. Die Multiplexer wählen aus, welches
  //   Ergebnis an die Ausgänge weitergeleitet
  //   wird, basierend auf das Vorzeichenbit aus
  //   Schritt 2.
endmodule

/* Test case:
a1 a0 b1 b0 y1 y0
loop(a, 4)
  loop(b,4)
    bits(2,a) bits(2,b) bits(2, ite(a > b, a-b, b-a))
  end loop
end loop
*/
