// Digital circuit 2_extend.dig as structural Verilog
module _2_extend (
  input  [11:0] in,
  output [31:0] out
);

  Multiplexer #(.Bits(20)) multiplexer_1 (.sel(in[11]), .in_0({20{1'b0}}), .in_1({20{1'b1}}), .out(out[31:12]));

  assign out[11:0] = {in[10:0], 1'b0};

  // Notes on the sheet:
  //   (alternativ mit der sign-extension Komponente lösbar)
endmodule

/* Test case TestExtend:
in out
let a=-10;
while(a < 10)
   let a=a+1;
   (a) (2*a)
end while
*/
