// Digital circuit 2_program_counter_simple.dig as structural Verilog
module _2_program_counter_simple (
  input  reset,
  input  clk
);

  wire [31:0] multiplexer_1_out, pc__plus__4_s, pc_q;

  Multiplexer #(.Bits(32)) multiplexer_1 (
    .sel(reset), .in_0(pc__plus__4_s), .in_1({32{1'b0}}), .out(multiplexer_1_out));
  Register #(.Bits(32)) pc (.D(multiplexer_1_out), .C(clk), .en(1'b1), .Q(pc_q));
  Add #(.Bits(32)) pc__plus__4 (.a(32'h4), .b(pc_q), .c_i(1'b0), .s(pc__plus__4_s));  // open: c_o
endmodule

/* Test case TestIncrReset:
clk reset pc
init pc=0;
0 0 0
repeat(10) C 0 (4*n+4)
C 1 0
*/

/* Test case TestOverflow:
clk reset pc
init pc=0xFFFFFFFF;
0 0 (0xFFFFFFFF)
C 0 (3)
*/
