// Digital circuit 2_program_counter_jump.dig as structural Verilog
module _2_program_counter_jump (
  input  reset,
  input  clk,
  input  pcsrc,
  input  [11:0] offset
);

  wire [31:0] multiplexer_1_out, pc_q;

  Multiplexer #(.Bits(32)) multiplexer_1 (.sel(reset), .in_1({32{1'b0}}), .out(multiplexer_1_out));  // open: in_0
  Register #(.Bits(32)) pc (.D(multiplexer_1_out), .C(clk), .en(1'b1), .Q(pc_q));
  Add #(.Bits(32)) pc__plus__4 (.a(32'h4), .b(pc_q), .c_i(1'b0));  // open: s, c_o
endmodule

/* Test case TestIncr:
clk reset pcsrc offset pc
init pc=0;
0 0 0 0 0
repeat(10) C 0 0 0 (4*n+4)
*/

/* Test case TestOffset:
clk reset pcsrc offset pc
init pc=0;
0 0 1 (5) 0
let a = 0;
while(a < 100)
   let incr = a + 1;
   let a = a + 2*incr;
   C 0 1 (incr) (a)
end while
*/
