// Digital circuit 2_bahnuebergang.dig as structural Verilog
module _2_bahnuebergang (
  input  S1,
  input  S2,
  input  clk,
  output M2,
  output M1
);

  wire multiplexer_1_out, not_1_out, not_2_out, not_3_out, not_4_out, notconnected_1_out, notconnected_2_out,
       notconnected_3_out;
  wire [3:0] add_1_s, d_ff_1_q, multiplexer_2_out;
  wire [8:2] rom_1_d;

  D_FF #(.Bits(4)) d_ff_1 (.D(multiplexer_2_out), .C(clk), .Q(d_ff_1_q));  // open: nQ
  // Probe on d_ff_1_q
  not not_1 (not_1_out, S2);
  not not_2 (not_2_out, S1);
  ROM #(.AddrBits(4), .Bits(9)) rom_1 (.A(d_ff_1_q), .sel(1'b1), .D({rom_1_d, M1, M2}));
  Add #(.Bits(4)) add_1 (.a(d_ff_1_q), .b(4'b0001), .c_i(1'b0), .s(add_1_s));  // open: c_o
  Multiplexer #(.Selector_Bits(3)) multiplexer_1 (
    .sel(rom_1_d[4:2]), .in_0(1'b1), .in_1(S1), .in_2(S2), .in_3(not_1_out), .in_4(not_2_out),
    .in_5(notconnected_1_out), .in_6(notconnected_2_out), .in_7(notconnected_3_out), .out(multiplexer_1_out));
  // NotConnected on notconnected_1_out
  // NotConnected on notconnected_2_out
  // NotConnected on notconnected_3_out
  not not_3 (not_3_out, M1);
  not not_4 (not_4_out, M2);
  Multiplexer #(.Bits(4)) multiplexer_2 (
    .sel(multiplexer_1_out), .in_0(add_1_s), .in_1(rom_1_d[8:5]), .out(multiplexer_2_out));
  LED led_1 (.in(M1));
  LED led_2 (.in(not_3_out));
  LED led_3 (.in(M2));
  LED led_4 (.in(not_4_out));

  // Notes on the sheet:
  //   contents of rom_1 (hex, n*v repeats v):
  //   64,c8,0,6f,8b,3,d3,e7,3
endmodule
