// Digital circuit 1_pattern_syn.dig as structural Verilog
module _1_pattern_syn (
  input  I,
  input  clk,
  output O
);

  wire not_1_out;

  not not_1 (not_1_out, I);
  D_FF FF1 (.C(clk));  // open: D, Q, nQ
  D_FF FF0 (.C(clk));  // open: D, Q, nQ
endmodule

/* Test case Test:
clk I FF1 FF0 O
init FF1=0;
init FF0=0;
0 0 0 0 0
C 0 0 0 0
C 1 0 1 0
C 1 0 1 0
C 0 1 0 0
C 0 0 0 0
C 1 0 1 0
C 0 1 0 0
C 1 1 1 1
C 0 1 0 0
C 1 1 1 1
C 1 0 1 0
*/
