// Logisim project abs.circ as structural Verilog: 1 circuit, main circuit main
module main (
  input  \a₁ ,
  input  \a₀ ,
  input  \b₁ ,
  input  \b₀ ,
  output out_5,
  output out_6,
  output out_7,
  output out_8,
  output Vorzeichen
);

  wire adder_1_cout, adder_2_cout, adder_4_cout, not_1_out, not_2_out, xor_1_out, xor_2_out;

  not not_1 (not_1_out, \b₀ );
  not not_2 (not_2_out, \b₁ );
  Adder #(.width(1)) adder_1 (.a(\a₀ ), .b(not_1_out), .out(out_5), .cin(1'b1), .cout(adder_1_cout));
  Adder #(.width(1)) adder_2 (.a(\a₁ ), .b(not_2_out), .out(out_7), .cin(adder_1_cout), .cout(adder_2_cout));
  Adder #(.width(1)) adder_3 (.a(1'b1), .b(1'b0), .out(Vorzeichen), .cin(adder_2_cout));  // open: cout
  xor xor_1 (xor_1_out, out_5, Vorzeichen);
  xor xor_2 (xor_2_out, out_7, Vorzeichen);
  Adder #(.width(1)) adder_4 (.a(1'b0), .b(xor_1_out), .out(out_6), .cin(Vorzeichen), .cout(adder_4_cout));
  Adder #(.width(1)) adder_5 (.a(1'b0), .b(xor_2_out), .out(out_8), .cin(adder_4_cout));  // open: cout

  // Notes on the sheet:
  //   (implizite dritte Stelle)
  //   1. Wir berechnen zuerst a-b
  //   mit zwei Addierern:
  //   Wir bringen also b ins
  //   Wir nehmen die Zahlen
  //   implizit als signed 3-Bit-Zahlen
  //   Zweierkomplement (Invertieren + 1)
  //   an, d.h. um das richtige Vorzeichen
  //   zu bekommen, müssen wir dies
  //   bei der dritten Stelle beachten
  //   Zwischenergebnis, Stelle 0
  //   Zwischenergebnis, Stelle 1
  //   (die XORs negieren die Werte,
  //   falls das Vorzeichen gesetzt ist)
  //   2. Wir wollen aber den
  //   Absolutbetrag von a-b
  //   d.h. falls ein Carry-Out produziert
  //   wurde (negative Zahl), müssen wir
  //   das Ergebnis noch zu einer
  //   positiven Zahl umwandeln
  //   (wieder mit Zweierkomplement)
  //   Endergebnis, Stelle 1
  //   Endergebnis, Stelle 0
  //   3. Wir erhalten unser
  //   erwünschtes Endergebnis
endmodule
